// Logisim project TP5-6.circ as structural Verilog: 1 circuit, main circuit SYSTEM
module SYSTEM (
  input  Rst,
  output out_2,
  output out_3,
  output port_keyboard
);

  wire Clk, clr_in, clr_out, comparator_1_eq, comparator_1_gt, comparator_2_gt, comparator_2_lt,
       comparator_4_eq, comparator_4_gt, comparator_5_eq, comparator_5_lt, hit, IO_ACK, IORD_REQ, IOWR_REQ,
       or_1_out, or_2_out, or_3_out, or_4_out, read, undriven, write;
  wire [6:0] char, key;
  wire [31:0] IO_ADDR, IO_DIN, undriven_2;
  wire [31:7] IO_DOUT;

  Clock u_clk (.out(Clk));
  Keyboard keyboard_1 (.clk(Clk), .re(read), .clr(clr_in), .avail(hit), .data(key));
  // Probe on key
  // Nios2Simulator nios2simulator_1: pin names not known; wires that end beside it: Clk, Rst, IO_ACK, {32{1'b0}}, 1'b0
  Comparator #(.width(32)) comparator_1 (
    .a(IO_ADDR), .b(32'h8000ff00), .gt(comparator_1_gt), .eq(comparator_1_eq));  // open: lt
  Comparator #(.width(32)) comparator_2 (
    .a(IO_ADDR), .b(32'h8000ff07), .gt(comparator_2_gt), .lt(comparator_2_lt));  // open: eq
  Comparator #(.width(32)) comparator_3 (.a(IO_ADDR), .b(32'h8000ff04), .eq(port_keyboard));  // open: gt, lt
  RAM #(.addrWidth(16), .dataWidth(32)) RAM_1 (.clr(IO_ADDR[2]));  // open: addr, data, sel, clk, ld
  or or_1 (or_1_out, comparator_1_gt, comparator_1_eq);
  or or_2 (or_2_out, comparator_2_gt, comparator_2_lt);
  Comparator #(.width(32)) comparator_4 (
    .a(IO_ADDR), .b(32'h80007040), .gt(comparator_4_gt), .eq(comparator_4_eq));  // open: lt
  Comparator #(.width(32)) comparator_5 (
    .a(IO_ADDR), .b(32'h80007043), .eq(comparator_5_eq), .lt(comparator_5_lt));  // open: gt
  and and_1 (clr_out, IO_DOUT[7], out_2);
  and and_2 (out_3, or_1_out, or_2_out);
  or or_3 (or_3_out, comparator_4_gt, comparator_4_eq);
  or or_4 (or_4_out, comparator_5_eq, comparator_5_lt);
  assign IO_DIN = undriven ? undriven_2 : 32'bz;  // Controlled_Buffer controlled_buffer_1
  // Probe on IO_ADDR
  // Probe on {IO_DOUT, char}
  // Probe on IO_DIN
  and and_3 (out_2, or_3_out, or_4_out);
  TTY tty_1 (.data(char), .clk(Clk), .we(write), .clr(clr_out));
  // FSM_Entity #(.content("state_machine CONSOLE @[116,36,800,500]{\n	in CS[1]   @[116,99,23,15];IOWR_REQ[1]   @[116,140,71,15];IORD_REQ[1]   @[116,177,69,15];\n	out WRITE[1]   @[872,140,44,15];IO_ACK[1]   @[867,192,49,15];\n	codeWidth = 2;\n	reset = S0;\n	\n	state S1[\"01\"]:\n	 	@[462,95,30,30]\n		set IO_ACK=\"1\";WRITE=IOWR_REQ;  @[462,95,30,30]	\n		goto S0  when default   @[601,272,43,22]; \n	state S0[\"00\"]:\n	 	@[455,397,30,30]\n		set IO_ACK=\"0\";  @[455,397,30,30]	\n		goto S1  when (CS.(IOWR_REQ+IORD_REQ))   @[198,294,177,22]; \n}")) fsm_entity_1: pin names not known; wires that end beside it: Clk, Rst, 1'b1, out_2, IOWR_REQ, IORD_REQ, write, IO_ACK
  // Pins of 1 and 16 bits meet at IO_ADDR[17:2]

  // Other names for the same wires on the sheet: IO_DOUT[6:0] = char

  // Notes on the sheet:
  //   TP 5-6 : entrées/sorties bus
  //   Périphérique clavier
  //   Processeur NIOS
  //   contents of RAM_1 (hex, n*v repeats v):
  //   1004004 100 600 3ffc26 deffff04 dfc00015 105883a 10c00007 19000004 400 18000226 10800044 3ffa26
  //   dfc00017 dec00104 f800283a deffff04 dfc00015 1600034 295c1004 29000025 dfc00017 dec00104 f800283a
  //   deffff04 dfc00015 1600034 295c1004 1800034 31802004 29800025 dfc00017 dec00104 f800283a 1200074
  //   213fc004 21400137 283ffe26 21400037 21400035 f800283a 23*0 6c6c6548 6f77206f 20646c72 6d6f7266
  //   4f494e20 49492053 6f727020 73736563 a726f 0 0 0 3f 6 5b 4f 66 6d 7d 7 7f 6f 77 7c 39 5e 79 71
  //   65442*0 28 8
  //   Périphérique console
endmodule
